# Fritzing sketch Sketch (saved by Fritzing 0.9.10b)
breadboards: 1

parts:
  J1 = Basic Servo
  Part1 = Arduino Uno (Rev3)

nets:
  GND: J1.gnd, Part1.GND
  VCC: J1.vcc, Part1.5V
  N1: J1.pulse, Part1.D9_PWM
